// Logisim project 1bit_swap.circ as structural Verilog: 1 circuit, main circuit swap
module swap (
  input  l1,
  input  l2,
  input  S,
  output O1,
  output O2
);

  wire and_1_out, and_2_out, and_3_out, and_4_out, and_5_out, not_1_out, not_2_out;

  not not_1 (not_1_out, S);
  and and_1 (and_1_out, 1'b1, not_1_out);
  and and_2 (and_2_out, l1, and_1_out);
  and and_3 (and_3_out, l2, and_1_out);
  not not_2 (not_2_out, and_1_out);
  and and_4 (and_4_out, l1, not_2_out);
  and and_5 (and_5_out, l2, not_2_out);
  or or_1 (O1, and_2_out, and_5_out);
  or or_2 (O2, and_3_out, and_4_out);
endmodule
