// Logisim project 4bit_sort.circ as structural Verilog: 1 circuit, main circuit main
module main (
  input  [3:0] in_1,
  input  [3:0] in_2,
  input  [3:0] in_3,
  input  [3:0] in_4,
  output [3:0] out_5,
  output [3:0] out_6,
  output [3:0] out_7,
  output [3:0] out_8
);

  wire comparator_1_gt, comparator_1_lt, comparator_2_gt, comparator_2_lt, comparator_3_gt, comparator_3_lt,
       comparator_4_gt, comparator_4_lt;
  wire [3:0] main_1_out_4, main_1_out_5, main_3_out_4, main_3_out_5;

  Comparator #(.width(4)) comparator_1 (.a(in_1), .b(in_2), .gt(comparator_1_gt), .lt(comparator_1_lt));  // open: eq
  Comparator #(.width(4)) comparator_2 (.a(in_3), .b(in_4), .gt(comparator_2_gt), .lt(comparator_2_lt));  // open: eq
  _4bit_swap_main main_1 (.in_1(in_2), .in_2(in_1), .in_3(comparator_1_gt), .out_4(main_1_out_4), .out_5(main_1_out_5));
  _4bit_swap_main main_2 (.in_1(in_1), .in_2(in_2), .in_3(comparator_1_lt), .out_4(main_1_out_4), .out_5(main_1_out_5));
  _4bit_swap_main main_3 (.in_1(in_4), .in_2(in_3), .in_3(comparator_2_gt), .out_4(main_3_out_4), .out_5(main_3_out_5));
  _4bit_swap_main main_4 (.in_1(in_3), .in_2(in_4), .in_3(comparator_2_lt), .out_4(main_3_out_4), .out_5(main_3_out_5));
  Comparator #(.width(4)) comparator_3 (
    .a(main_1_out_4), .b(main_3_out_4), .gt(comparator_3_gt), .lt(comparator_3_lt));  // open: eq
  Comparator #(.width(4)) comparator_4 (
    .a(main_1_out_5), .b(main_3_out_5), .gt(comparator_4_gt), .lt(comparator_4_lt));  // open: eq
  _4bit_swap_main main_5 (
    .in_1(main_3_out_4), .in_2(main_1_out_4), .in_3(comparator_3_gt), .out_4(out_5), .out_5(out_6));
  _4bit_swap_main main_6 (
    .in_1(main_1_out_4), .in_2(main_3_out_4), .in_3(comparator_3_lt), .out_4(out_5), .out_5(out_6));
  _4bit_swap_main main_7 (
    .in_1(main_3_out_5), .in_2(main_1_out_5), .in_3(comparator_4_gt), .out_4(out_7), .out_5(out_8));
  _4bit_swap_main main_8 (
    .in_1(main_1_out_5), .in_2(main_3_out_5), .in_3(comparator_4_lt), .out_4(out_7), .out_5(out_8));
endmodule
