// Logisim project 4bit_swap.circ as structural Verilog: 1 circuit, main circuit main
module main (
  input  [3:0] in_1,
  input  [3:0] in_2,
  input  in_3,
  output [3:0] out_4,
  output [3:0] out_5
);

  swap swap_1 (.l1(in_1[0]), .l2(in_2[0]), .S(in_3), .O1(out_4[0]), .O2(out_5[0]));
  swap swap_2 (.l1(in_1[1]), .l2(in_2[1]), .S(in_3), .O1(out_4[1]), .O2(out_5[1]));
  swap swap_3 (.l1(in_1[2]), .l2(in_2[2]), .S(in_3), .O1(out_4[2]), .O2(out_5[2]));
  swap swap_4 (.l1(in_1[3]), .l2(in_2[3]), .S(in_3), .O1(out_4[3]), .O2(out_5[3]));
endmodule
