// Logisim project CRC.circ as structural Verilog
module mod2div (
  input  [3:0] \被除数 ,
  input  [3:0] \除数 ,
  output [2:0] \余数 ,
  output \商 
);

  wire and_1_out;
  wire [3:0] xor_1_out;

  assign xor_1_out = \除数  ^ \被除数 ;  // XOR_Gate xor_1, 4 bits wide
  and and_1 (and_1_out, 1'b1, \被除数 [3]);
  Multiplexer multiplexer_1 (.in0(1'b0), .in1(1'b1), .out(\商 ), .sel(and_1_out), .en(1'b1));
  Multiplexer #(.width(3)) multiplexer_2 (
    .in0(\被除数 [2:0]), .in1(xor_1_out[2:0]), .out(\余数 ), .sel(and_1_out), .en(1'b1));
endmodule

module CRC (
  input  [7:0] in_1,
  input  [3:0] in_2,
  output [10:0] out_3
);

  wire [2:0] \mod2div_1_余数 , \mod2div_2_余数 , \mod2div_3_余数 , \mod2div_5_余数 , \mod2div_6_余数 , \mod2div_7_余数 ;
  wire [3:1] \mod2div_4_余数 ;

  mod2div mod2div_1 (.\被除数 (in_1[7:4]), .\除数 (in_2), .\余数 (\mod2div_1_余数 ));  // open: 商
  mod2div mod2div_2 (.\被除数 ({\mod2div_1_余数 , in_1[3]}), .\除数 (in_2), .\余数 (\mod2div_2_余数 ));  // open: 商
  mod2div mod2div_3 (.\被除数 ({\mod2div_2_余数 , in_1[2]}), .\除数 (in_2), .\余数 (\mod2div_3_余数 ));  // open: 商
  mod2div mod2div_4 (.\被除数 ({\mod2div_3_余数 , in_1[1]}), .\除数 (in_2), .\余数 (\mod2div_4_余数 ));  // open: 商
  mod2div mod2div_5 (.\被除数 ({\mod2div_4_余数 , in_1[0]}), .\除数 (in_2), .\余数 (\mod2div_5_余数 ));  // open: 商
  mod2div mod2div_6 (.\被除数 ({\mod2div_5_余数 , 1'b0}), .\除数 (in_2), .\余数 (\mod2div_6_余数 ));  // open: 商
  mod2div mod2div_7 (.\被除数 ({\mod2div_6_余数 , 1'b0}), .\除数 (in_2), .\余数 (\mod2div_7_余数 ));  // open: 商
  mod2div mod2div_8 (.\被除数 ({\mod2div_7_余数 , 1'b0}), .\除数 (in_2), .\余数 (out_3[2:0]));  // open: 商

  assign out_3[10:3] = in_1;
endmodule
