// Logisim project FB-Final.circ as structural Verilog: 4 circuits, main circuit main
module main (
  input  [31:0] in_1,
  output [31:0] out_2
);

  wire and_1_out, clock_1_out, comparator_1_lt, comparator_2_eq, comparator_2_gt, comparator_3_eq,
       comparator_3_gt, comparator_4_eq, comparator_4_gt, comparator_5_gt, comparator_6_eq, comparator_6_lt,
       judge_jishu_1_out_2, not_1_out, or_1_out, or_2_out, or_3_out;
  wire [4:0] multiplexer_10_out;
  wire [7:0] counter_1_q, counter_4_q;
  wire [31:0] COT_TEMP_r00, COT_TEMP_r01, COT_TEMP_r10, COT_TEMP_r11, counter_2_q, counter_3_q,
       multiplexer_1_out, multiplexer_2_out, multiplexer_3_out, multiplexer_4_out, multiplexer_5_out,
       multiplexer_6_out, multiplexer_7_out, multiplexer_8_out, multiplexer_9_out, New_COT00_q, New_COT01_q,
       New_COT10_q, New_COT11_q, New_TEMP00_q, New_TEMP01_q, New_TEMP10_q, New_TEMP11_q, register_1_q,
       shifter_1_out, TEMP_TEMP_r00, TEMP_TEMP_r01, TEMP_TEMP_r10, TEMP_TEMP_r11;

  Clock clock_1 (.out(clock_1_out));
  Counter counter_1 (.Q(counter_1_q), .clk(clock_1_out));  // open: load, D, count, carry, clr
  Multiplexer #(.width(32)) multiplexer_1 (
    .in0(32'h1), .in1(New_TEMP00_q), .out(multiplexer_1_out), .sel(not_1_out), .en(1'b1));
  Multiplexer #(.width(32)) multiplexer_2 (
    .in0(32'h1), .in1(New_TEMP01_q), .out(multiplexer_2_out), .sel(not_1_out), .en(1'b1));
  Multiplexer #(.width(32)) multiplexer_3 (
    .in0(32'h1), .in1(New_TEMP10_q), .out(multiplexer_3_out), .sel(not_1_out), .en(1'b1));
  Multiplexer #(.width(32)) multiplexer_4 (
    .in0({32{1'b0}}), .in1(New_TEMP11_q), .out(multiplexer_4_out), .sel(not_1_out), .en(1'b1));
  Multiplexer #(.width(32)) multiplexer_5 (
    .in0(32'h1), .in1(New_COT00_q), .out(multiplexer_5_out), .sel(or_3_out), .en(1'b1));
  Multiplexer #(.width(32)) multiplexer_6 (
    .in0({32{1'b0}}), .in1(New_COT01_q), .out(multiplexer_6_out), .sel(or_3_out), .en(1'b1));
  Multiplexer #(.width(32)) multiplexer_7 (
    .in0({32{1'b0}}), .in1(New_COT10_q), .out(multiplexer_7_out), .sel(or_3_out), .en(1'b1));
  Multiplexer #(.width(32)) multiplexer_8 (
    .in0(32'h1), .in1(New_COT11_q), .out(multiplexer_8_out), .sel(or_3_out), .en(1'b1));
  Comparator #(.mode("unsigned")) comparator_1 (.a(counter_1_q), .b(8'h1), .lt(comparator_1_lt));  // open: gt, eq
  Comparator comparator_2 (.a(counter_1_q), .b(8'h22), .gt(comparator_2_gt), .eq(comparator_2_eq));  // open: lt
  Multiplexer #(.width(32)) multiplexer_9 (
    .in0(shifter_1_out), .in1(in_1), .out(multiplexer_9_out), .sel(comparator_1_lt), .en(1'b1));
  Register #(.width(32)) register_1 (.D(multiplexer_9_out), .Q(register_1_q), .clk(clock_1_out));  // open: en, clr
  or or_1 (or_1_out, comparator_2_gt, comparator_2_eq);
  Shifter #(.width(32), .shift("lr")) shifter_1 (.in(register_1_q), .\dist (multiplexer_10_out), .out(shifter_1_out));
  Square_Mult TEMP_TEMP (
    .A00(multiplexer_1_out), .A01(multiplexer_2_out), .A10(multiplexer_3_out), .A11(multiplexer_4_out),
    .B00(multiplexer_1_out), .B01(multiplexer_2_out), .B10(multiplexer_3_out), .B11(multiplexer_4_out),
    .R00(TEMP_TEMP_r00), .R01(TEMP_TEMP_r01), .R10(TEMP_TEMP_r10), .R11(TEMP_TEMP_r11));
  Square_Mult_Select COT_TEMP (
    .A00(multiplexer_5_out), .A01(multiplexer_6_out), .A10(multiplexer_7_out), .A11(multiplexer_8_out),
    .B00(multiplexer_1_out), .B01(multiplexer_2_out), .B10(multiplexer_3_out), .B11(multiplexer_4_out),
    .Enabled(judge_jishu_1_out_2), .C00(New_COT00_q), .C01(New_COT01_q), .C10(New_COT10_q),
    .C11(New_COT11_q), .R00(COT_TEMP_r00), .R01(COT_TEMP_r01), .R10(COT_TEMP_r10), .R11(COT_TEMP_r11));
  Counter #(.width(32), .max('hffffffff)) counter_2 (
    .Q(counter_2_q), .clk(clock_1_out));  // open: load, D, count, carry, clr
  Comparator #(.width(32), .mode("unsigned")) comparator_3 (
    .a(register_1_q), .b({32{1'b0}}), .gt(comparator_3_gt), .eq(comparator_3_eq));  // open: lt
  Multiplexer #(.width(5)) multiplexer_10 (
    .in0(5'b00001), .in1({5{1'b0}}), .out(multiplexer_10_out), .sel(comparator_5_gt), .en(1'b1));
  Register #(.width(32)) New_TEMP00 (
    .D(TEMP_TEMP_r00), .en(comparator_3_gt), .Q(New_TEMP00_q), .clk(clock_1_out));  // open: clr
  Register #(.width(32)) New_TEMP01 (
    .D(TEMP_TEMP_r01), .en(comparator_3_gt), .Q(New_TEMP01_q), .clk(clock_1_out));  // open: clr
  Register #(.width(32)) New_TEMP10 (
    .D(TEMP_TEMP_r10), .en(comparator_3_gt), .Q(New_TEMP10_q), .clk(clock_1_out));  // open: clr
  Register #(.width(32)) New_TEMP11 (
    .D(TEMP_TEMP_r11), .en(comparator_3_gt), .Q(New_TEMP11_q), .clk(clock_1_out));  // open: clr
  Register #(.width(32)) New_COT00 (
    .D(COT_TEMP_r00), .en(comparator_3_gt), .Q(New_COT00_q), .clk(clock_1_out));  // open: clr
  Register #(.width(32)) New_COT01 (
    .D(COT_TEMP_r01), .en(comparator_3_gt), .Q(New_COT01_q), .clk(clock_1_out));  // open: clr
  Register #(.width(32)) New_COT10 (
    .D(COT_TEMP_r10), .en(comparator_3_gt), .Q(New_COT10_q), .clk(clock_1_out));  // open: clr
  Register #(.width(32)) New_COT11 (
    .D(COT_TEMP_r11), .en(comparator_3_gt), .Q(New_COT11_q), .clk(clock_1_out));  // open: clr
  Comparator #(.width(32), .mode("unsigned")) comparator_4 (
    .a(32'h1), .b(counter_2_q), .gt(comparator_4_gt), .eq(comparator_4_eq));  // open: lt
  Counter #(.width(32), .max('hffffffff)) counter_3 (
    .Q(counter_3_q), .clk(comparator_3_eq));  // open: load, D, count, carry, clr
  or or_2 (or_2_out, comparator_4_gt, comparator_4_eq);
  Counter counter_4 (.Q(counter_4_q), .clk(and_1_out));  // open: load, D, count, carry, clr
  not not_1 (not_1_out, or_2_out);
  Comparator #(.width(32), .mode("unsigned")) comparator_5 (
    .a(counter_3_q), .b({32{1'b0}}), .gt(comparator_5_gt));  // open: eq, lt
  and and_1 (and_1_out, judge_jishu_1_out_2, clock_1_out);
  Judge_Jishu judge_jishu_1 (.in_1(register_1_q), .out_2(judge_jishu_1_out_2));
  or or_3 (or_3_out, comparator_6_eq, comparator_6_lt);
  Comparator #(.mode("unsigned")) comparator_6 (
    .a(8'h2), .b(counter_4_q), .eq(comparator_6_eq), .lt(comparator_6_lt));  // open: gt
  Multiplexer #(.width(32)) multiplexer_11 (
    .in0({32{1'b0}}), .in1(New_COT01_q), .out(out_2), .sel(or_1_out), .en(1'b1));
endmodule

module Square_Mult (
  input  [31:0] A00,
  input  [31:0] A01,
  input  [31:0] A10,
  input  [31:0] A11,
  input  [31:0] B00,
  input  [31:0] B01,
  input  [31:0] B10,
  input  [31:0] B11,
  output [31:0] R00,
  output [31:0] R01,
  output [31:0] R10,
  output [31:0] R11
);

  wire [31:0] multiplier_1_out, multiplier_2_out, multiplier_3_out, multiplier_4_out, multiplier_5_out,
       multiplier_6_out, multiplier_7_out, multiplier_8_out;

  Multiplier #(.width(32)) multiplier_1 (.a(A00), .b(B00), .out(multiplier_1_out));  // open: cin, cout
  Multiplier #(.width(32)) multiplier_2 (.a(A01), .b(B01), .out(multiplier_2_out));  // open: cin, cout
  Multiplier #(.width(32)) multiplier_3 (.a(A00), .b(B01), .out(multiplier_3_out));  // open: cin, cout
  Multiplier #(.width(32)) multiplier_4 (.a(A01), .b(B11), .out(multiplier_4_out));  // open: cin, cout
  Multiplier #(.width(32)) multiplier_5 (.a(A11), .b(B10), .out(multiplier_5_out));  // open: cin, cout
  Multiplier #(.width(32)) multiplier_6 (.a(B00), .b(A10), .out(multiplier_6_out));  // open: cin, cout
  Multiplier #(.width(32)) multiplier_7 (.a(A10), .b(B01), .out(multiplier_7_out));  // open: cin, cout
  Multiplier #(.width(32)) multiplier_8 (.a(A11), .b(B11), .out(multiplier_8_out));  // open: cin, cout
  Adder #(.width(32)) adder_1 (.a(multiplier_1_out), .b(multiplier_2_out), .out(R00));  // open: cin, cout
  Adder #(.width(32)) adder_2 (.a(multiplier_3_out), .b(multiplier_4_out), .out(R01));  // open: cin, cout
  Adder #(.width(32)) adder_3 (.a(multiplier_5_out), .b(multiplier_6_out), .out(R10));  // open: cin, cout
  Adder #(.width(32)) adder_4 (.a(multiplier_7_out), .b(multiplier_8_out), .out(R11));  // open: cin, cout
endmodule

module Square_Mult_Select (
  input  [31:0] A00,
  input  [31:0] A01,
  input  [31:0] A10,
  input  [31:0] A11,
  input  [31:0] B00,
  input  [31:0] B01,
  input  [31:0] B10,
  input  [31:0] B11,
  input  Enabled,
  input  [31:0] C00,
  input  [31:0] C01,
  input  [31:0] C10,
  input  [31:0] C11,
  output [31:0] R00,
  output [31:0] R01,
  output [31:0] R10,
  output [31:0] R11
);

  wire [31:0] adder_1_out, adder_2_out, adder_3_out, adder_4_out, multiplier_1_out, multiplier_2_out,
       multiplier_3_out, multiplier_4_out, multiplier_5_out, multiplier_6_out, multiplier_7_out,
       multiplier_8_out;

  Multiplier #(.width(32)) multiplier_1 (.a(A00), .b(B00), .out(multiplier_1_out));  // open: cin, cout
  Multiplier #(.width(32)) multiplier_2 (.a(A01), .b(B01), .out(multiplier_2_out));  // open: cin, cout
  Multiplier #(.width(32)) multiplier_3 (.a(A00), .b(B01), .out(multiplier_3_out));  // open: cin, cout
  Multiplier #(.width(32)) multiplier_4 (.a(A01), .b(B11), .out(multiplier_4_out));  // open: cin, cout
  Multiplier #(.width(32)) multiplier_5 (.a(A11), .b(B10), .out(multiplier_5_out));  // open: cin, cout
  Multiplier #(.width(32)) multiplier_6 (.a(B00), .b(A10), .out(multiplier_6_out));  // open: cin, cout
  Multiplier #(.width(32)) multiplier_7 (.a(A10), .b(B01), .out(multiplier_7_out));  // open: cin, cout
  Multiplier #(.width(32)) multiplier_8 (.a(A11), .b(B11), .out(multiplier_8_out));  // open: cin, cout
  Adder #(.width(32)) adder_1 (.a(multiplier_1_out), .b(multiplier_2_out), .out(adder_1_out));  // open: cin, cout
  Adder #(.width(32)) adder_2 (.a(multiplier_3_out), .b(multiplier_4_out), .out(adder_2_out));  // open: cin, cout
  Adder #(.width(32)) adder_3 (.a(multiplier_5_out), .b(multiplier_6_out), .out(adder_3_out));  // open: cin, cout
  Adder #(.width(32)) adder_4 (.a(multiplier_7_out), .b(multiplier_8_out), .out(adder_4_out));  // open: cin, cout
  Multiplexer #(.width(32)) multiplexer_1 (.in0(C00), .in1(adder_1_out), .out(R00), .sel(Enabled), .en(1'b1));
  Multiplexer #(.width(32)) multiplexer_2 (.in0(C01), .in1(adder_2_out), .out(R01), .sel(Enabled), .en(1'b1));
  Multiplexer #(.width(32)) multiplexer_3 (.in0(C10), .in1(adder_3_out), .out(R10), .sel(Enabled), .en(1'b1));
  Multiplexer #(.width(32)) multiplexer_4 (.in0(C11), .in1(adder_4_out), .out(R11), .sel(Enabled), .en(1'b1));
endmodule

module Judge_Jishu (
  input  [31:0] in_1,
  output out_2
);

  and and_1 (out_2, 1'b1, in_1[0]);
endmodule
