// Logisim project FB.circ as structural Verilog: 2 circuits, main circuit main
module main (
  input  [2:0] in_1,
  output [3:0] out_2
);

  wire clock_1_out, comparator_1_eq, comparator_2_lt, comparator_3_eq, comparator_4_eq, comparator_4_gt,
       comparator_4_lt, comparator_5_eq, comparator_6_gt, not_1_out, or_1_out;
  wire [2:0] judge_t_1_out_3, register_1_q;
  wire [3:0] adder_1_out, First_q, multiplexer_1_out, multiplexer_2_out, multiplexer_3_out, register_2_q,
       Second_q, subtractor_1_out;
  wire [7:0] counter_1_q, counter_2_q;

  Register #(.width(3)) register_1 (.D(in_1), .Q(register_1_q), .clk(clock_1_out));  // open: en, clr
  judge_T judge_t_1 (
    .In_1(in_1[2]), .In_2(in_1[1]), .In_3(in_1[0]), .Out_1(judge_t_1_out_3[2]), .Out_2(judge_t_1_out_3[1]),
    .Out_3(judge_t_1_out_3[0]));
  Comparator #(.width(3), .mode("unsigned")) comparator_1 (
    .a(register_1_q), .b(in_1), .eq(comparator_1_eq));  // open: gt, lt
  not not_1 (not_1_out, comparator_1_eq);
  Clock clock_1 (.out(clock_1_out));
  Counter counter_1 (.Q(counter_1_q), .clk(clock_1_out), .clr(not_1_out));  // open: load, D, count, carry
  Comparator comparator_2 (.a(counter_1_q), .b(8'h1), .lt(comparator_2_lt));  // open: gt, eq
  Multiplexer #(.width(4)) multiplexer_1 (
    .in0(subtractor_1_out), .in1({1'b0, judge_t_1_out_3}), .out(multiplexer_1_out), .sel(comparator_2_lt),
    .en(1'b1));
  Register #(.width(4)) register_2 (.D(multiplexer_1_out), .Q(register_2_q), .clk(clock_1_out));  // open: en, clr
  Subtractor #(.width(4)) subtractor_1 (
    .a(register_2_q), .b(multiplexer_2_out), .out(subtractor_1_out));  // open: bin, bout
  Register #(.width(4)) First (.D(Second_q), .en(comparator_4_gt), .Q(First_q), .clk(clock_1_out), .clr(not_1_out));
  Comparator #(.width(4), .mode("unsigned")) comparator_3 (
    .a(First_q), .b(4'b0000), .eq(comparator_3_eq));  // open: gt, lt
  Multiplexer #(.width(4)) multiplexer_2 (
    .in0(4'b0001), .in1(4'b0000), .out(multiplexer_2_out), .sel(comparator_6_gt), .en(1'b1));
  Multiplexer #(.width(4)) multiplexer_3 (
    .in0(adder_1_out), .in1(4'b0001), .out(multiplexer_3_out), .sel(comparator_3_eq), .en(1'b1));
  Register #(.width(4)) Second (
    .D(multiplexer_3_out), .en(comparator_4_gt), .Q(Second_q), .clk(clock_1_out), .clr(not_1_out));
  Comparator #(.width(4)) comparator_4 (
    .a(register_2_q), .b(4'b0000), .gt(comparator_4_gt), .eq(comparator_4_eq), .lt(comparator_4_lt));
  Adder #(.width(4)) adder_1 (.a(First_q), .b(Second_q), .out(adder_1_out));  // open: cin, cout
  Comparator #(.width(3), .mode("unsigned")) comparator_5 (.a(in_1), .b(3'b000), .eq(comparator_5_eq));  // open: gt, lt
  or or_1 (or_1_out, comparator_4_eq, comparator_4_lt);
  Multiplexer #(.width(4)) multiplexer_4 (.in0(Second_q), .in1(4'b0000), .out(out_2), .sel(comparator_5_eq), .en(1'b1));
  Counter counter_2 (.Q(counter_2_q), .clk(or_1_out), .clr(not_1_out));  // open: load, D, count, carry
  Comparator #(.mode("unsigned")) comparator_6 (.a(counter_2_q), .b({8{1'b0}}), .gt(comparator_6_gt));  // open: eq, lt
endmodule

module judge_T (
  input  In_1,
  input  In_2,
  input  In_3,
  output Out_1,
  output Out_2,
  output Out_3
);

  wire and_1_out, and_2_out, and_3_out, and_4_out, and_5_out, and_6_out, and_7_out, not_1_out, not_2_out,
       not_3_out, not_4_out, not_5_out, not_6_out;

  and and_1 (and_1_out, In_1, In_3);
  and and_2 (and_2_out, In_1, In_2);
  not not_1 (not_1_out, In_2);
  not not_2 (not_2_out, In_3);
  not not_3 (not_3_out, In_1);
  not not_4 (not_4_out, In_2);
  not not_5 (not_5_out, In_3);
  not not_6 (not_6_out, In_3);
  or or_1 (Out_1, and_1_out, and_2_out);
  and and_3 (and_3_out, In_2, In_3);
  and and_4 (and_4_out, In_1, not_1_out, not_2_out);
  and and_5 (and_5_out, not_3_out, not_4_out, In_3);
  and and_6 (and_6_out, In_2, not_5_out);
  and and_7 (and_7_out, In_1, not_6_out);
  or or_2 (Out_2, and_3_out, and_4_out);
  or or_3 (Out_3, and_5_out, and_6_out, and_7_out);
endmodule
