// Logisim project Signal-Turn CPU.circ as structural Verilog: 7 circuits, main circuit main
module Choose (
  input  in_1,
  input  [4:0] in_2,
  output out_3,
  output out_4,
  output out_5,
  output out_6,
  output out_7,
  output out_8,
  output out_9,
  output out_10,
  output out_11,
  output out_12,
  output out_13,
  output out_14,
  output out_15,
  output out_16,
  output out_17,
  output out_18,
  output out_19,
  output out_20,
  output out_21,
  output out_22,
  output out_23,
  output out_24,
  output out_25,
  output out_26,
  output out_27,
  output out_28,
  output out_29,
  output out_30,
  output out_31,
  output out_32,
  output out_33,
  output out_34
);

  wire comparator_1_eq, comparator_2_eq, comparator_3_eq, comparator_4_eq, comparator_5_eq, comparator_6_eq,
       comparator_7_eq, comparator_8_eq, comparator_9_eq, comparator_10_eq, comparator_11_eq,
       comparator_12_eq, comparator_13_eq, comparator_14_eq, comparator_15_eq, comparator_16_eq,
       comparator_17_eq, comparator_18_eq, comparator_19_eq, comparator_20_eq, comparator_21_eq,
       comparator_22_eq, comparator_23_eq, comparator_24_eq, comparator_25_eq, comparator_26_eq,
       comparator_27_eq, comparator_28_eq, comparator_29_eq, comparator_30_eq, comparator_31_eq,
       comparator_32_eq;

  Comparator #(.width(5), .mode("unsigned")) comparator_1 (
    .a({5{1'b0}}), .b(in_2), .eq(comparator_1_eq));  // open: gt, lt
  Comparator #(.width(5), .mode("unsigned")) comparator_2 (
    .a(5'b00001), .b(in_2), .eq(comparator_2_eq));  // open: gt, lt
  Comparator #(.width(5), .mode("unsigned")) comparator_3 (
    .a(5'b00010), .b(in_2), .eq(comparator_3_eq));  // open: gt, lt
  Comparator #(.width(5), .mode("unsigned")) comparator_4 (
    .a(5'b00011), .b(in_2), .eq(comparator_4_eq));  // open: gt, lt
  Comparator #(.width(5), .mode("unsigned")) comparator_5 (
    .a(5'b00100), .b(in_2), .eq(comparator_5_eq));  // open: gt, lt
  Comparator #(.width(5), .mode("unsigned")) comparator_6 (
    .a(5'b00101), .b(in_2), .eq(comparator_6_eq));  // open: gt, lt
  Comparator #(.width(5), .mode("unsigned")) comparator_7 (
    .a(5'b00110), .b(in_2), .eq(comparator_7_eq));  // open: gt, lt
  Comparator #(.width(5), .mode("unsigned")) comparator_8 (
    .a(5'b00111), .b(in_2), .eq(comparator_8_eq));  // open: gt, lt
  Comparator #(.width(5), .mode("unsigned")) comparator_9 (
    .a(5'b01000), .b(in_2), .eq(comparator_9_eq));  // open: gt, lt
  Comparator #(.width(5), .mode("unsigned")) comparator_10 (
    .a(5'b01001), .b(in_2), .eq(comparator_10_eq));  // open: gt, lt
  Comparator #(.width(5), .mode("unsigned")) comparator_11 (
    .a(5'b01010), .b(in_2), .eq(comparator_11_eq));  // open: gt, lt
  Comparator #(.width(5), .mode("unsigned")) comparator_12 (
    .a(5'b01011), .b(in_2), .eq(comparator_12_eq));  // open: gt, lt
  Comparator #(.width(5), .mode("unsigned")) comparator_13 (
    .a(5'b01100), .b(in_2), .eq(comparator_13_eq));  // open: gt, lt
  Comparator #(.width(5), .mode("unsigned")) comparator_14 (
    .a(5'b01101), .b(in_2), .eq(comparator_14_eq));  // open: gt, lt
  Comparator #(.width(5), .mode("unsigned")) comparator_15 (
    .a(5'b01110), .b(in_2), .eq(comparator_15_eq));  // open: gt, lt
  Comparator #(.width(5), .mode("unsigned")) comparator_16 (
    .a(5'b01111), .b(in_2), .eq(comparator_16_eq));  // open: gt, lt
  Comparator #(.width(5), .mode("unsigned")) comparator_17 (
    .a(5'b10000), .b(in_2), .eq(comparator_17_eq));  // open: gt, lt
  Comparator #(.width(5), .mode("unsigned")) comparator_18 (
    .a(5'b10001), .b(in_2), .eq(comparator_18_eq));  // open: gt, lt
  Comparator #(.width(5), .mode("unsigned")) comparator_19 (
    .a(5'b10010), .b(in_2), .eq(comparator_19_eq));  // open: gt, lt
  Comparator #(.width(5), .mode("unsigned")) comparator_20 (
    .a(5'b10011), .b(in_2), .eq(comparator_20_eq));  // open: gt, lt
  Comparator #(.width(5), .mode("unsigned")) comparator_21 (
    .a(5'b10100), .b(in_2), .eq(comparator_21_eq));  // open: gt, lt
  Comparator #(.width(5), .mode("unsigned")) comparator_22 (
    .a(5'b10101), .b(in_2), .eq(comparator_22_eq));  // open: gt, lt
  Comparator #(.width(5), .mode("unsigned")) comparator_23 (
    .a(5'b10110), .b(in_2), .eq(comparator_23_eq));  // open: gt, lt
  Comparator #(.width(5), .mode("unsigned")) comparator_24 (
    .a(5'b10111), .b(in_2), .eq(comparator_24_eq));  // open: gt, lt
  Comparator #(.width(5), .mode("unsigned")) comparator_25 (
    .a(5'b11000), .b(in_2), .eq(comparator_25_eq));  // open: gt, lt
  Comparator #(.width(5), .mode("unsigned")) comparator_26 (
    .a(5'b11001), .b(in_2), .eq(comparator_26_eq));  // open: gt, lt
  Comparator #(.width(5), .mode("unsigned")) comparator_27 (
    .a(5'b11010), .b(in_2), .eq(comparator_27_eq));  // open: gt, lt
  Comparator #(.width(5), .mode("unsigned")) comparator_28 (
    .a(5'b11011), .b(in_2), .eq(comparator_28_eq));  // open: gt, lt
  Comparator #(.width(5), .mode("unsigned")) comparator_29 (
    .a(5'b11100), .b(in_2), .eq(comparator_29_eq));  // open: gt, lt
  Comparator #(.width(5), .mode("unsigned")) comparator_30 (
    .a(5'b11101), .b(in_2), .eq(comparator_30_eq));  // open: gt, lt
  Comparator #(.width(5), .mode("unsigned")) comparator_31 (
    .a(5'b11110), .b(in_2), .eq(comparator_31_eq));  // open: gt, lt
  Comparator #(.width(5), .mode("unsigned")) comparator_32 (
    .a({5{1'b1}}), .b(in_2), .eq(comparator_32_eq));  // open: gt, lt
  and and_1 (out_3, in_1, comparator_1_eq);
  and and_2 (out_4, in_1, comparator_2_eq);
  and and_3 (out_5, in_1, comparator_3_eq);
  and and_4 (out_6, in_1, comparator_4_eq);
  and and_5 (out_7, in_1, comparator_5_eq);
  and and_6 (out_8, in_1, comparator_6_eq);
  and and_7 (out_9, in_1, comparator_7_eq);
  and and_8 (out_10, in_1, comparator_8_eq);
  and and_9 (out_11, in_1, comparator_9_eq);
  and and_10 (out_12, in_1, comparator_10_eq);
  and and_11 (out_13, comparator_11_eq, in_1);
  and and_12 (out_14, comparator_12_eq, in_1);
  and and_13 (out_15, comparator_13_eq, in_1);
  and and_14 (out_16, comparator_14_eq, in_1);
  and and_15 (out_17, comparator_15_eq, in_1);
  and and_16 (out_18, comparator_16_eq, in_1);
  and and_17 (out_19, comparator_17_eq, in_1);
  and and_18 (out_20, comparator_18_eq, in_1);
  and and_19 (out_21, comparator_19_eq, in_1);
  and and_20 (out_22, comparator_20_eq, in_1);
  and and_21 (out_23, comparator_21_eq, in_1);
  and and_22 (out_24, comparator_22_eq, in_1);
  and and_23 (out_25, comparator_23_eq, in_1);
  and and_24 (out_26, comparator_24_eq, in_1);
  and and_25 (out_27, comparator_25_eq, in_1);
  and and_26 (out_28, comparator_26_eq, in_1);
  and and_27 (out_29, comparator_27_eq, in_1);
  and and_28 (out_30, comparator_28_eq, in_1);
  and and_29 (out_31, comparator_29_eq, in_1);
  and and_30 (out_32, comparator_30_eq, in_1);
  and and_31 (out_33, comparator_31_eq, in_1);
  and and_32 (out_34, comparator_32_eq, in_1);
endmodule

module choose_output (
  input  [4:0] A1,
  input  [31:0] in_2,
  input  [31:0] in_3,
  input  [31:0] in_4,
  input  [31:0] in_5,
  input  [31:0] in_6,
  input  [31:0] in_7,
  input  [31:0] in_8,
  input  [31:0] in_9,
  input  [31:0] in_10,
  input  [31:0] in_11,
  input  [31:0] in_12,
  input  [31:0] in_13,
  input  [31:0] in_14,
  input  [31:0] in_15,
  input  [31:0] in_16,
  input  [31:0] in_17,
  input  [31:0] in_18,
  input  [31:0] in_19,
  input  [31:0] in_20,
  input  [31:0] in_21,
  input  [31:0] in_22,
  input  [31:0] in_23,
  input  [31:0] in_24,
  input  [31:0] in_25,
  input  [31:0] in_26,
  input  [31:0] in_27,
  input  [31:0] in_28,
  input  [31:0] in_29,
  input  [31:0] in_30,
  input  [31:0] in_31,
  input  [31:0] in_32,
  input  [31:0] in_33,
  output [31:0] out_34
);

  wire choose_1_out_3, choose_1_out_4, choose_1_out_5, choose_1_out_6, choose_1_out_7, choose_1_out_8,
       choose_1_out_9, choose_1_out_10, choose_1_out_11, choose_1_out_12, choose_1_out_13, choose_1_out_14,
       choose_1_out_15, choose_1_out_16, choose_1_out_17, choose_1_out_18, choose_1_out_19, choose_1_out_20,
       choose_1_out_21, choose_1_out_22, choose_1_out_23, choose_1_out_24, choose_1_out_25, choose_1_out_26,
       choose_1_out_27, choose_1_out_28, choose_1_out_29, choose_1_out_30, choose_1_out_31, choose_1_out_32,
       choose_1_out_33, choose_1_out_34;
  wire [31:0] multiplexer_1_out, multiplexer_2_out, multiplexer_3_out, multiplexer_4_out, multiplexer_5_out,
       multiplexer_6_out, multiplexer_7_out, multiplexer_8_out, multiplexer_9_out, multiplexer_10_out,
       multiplexer_11_out, multiplexer_12_out, multiplexer_13_out, multiplexer_14_out, multiplexer_15_out,
       multiplexer_16_out, multiplexer_17_out, multiplexer_18_out, multiplexer_19_out, multiplexer_20_out,
       multiplexer_21_out, multiplexer_22_out, multiplexer_23_out, multiplexer_24_out, multiplexer_25_out,
       multiplexer_26_out, multiplexer_27_out, multiplexer_28_out, multiplexer_29_out, multiplexer_30_out,
       multiplexer_31_out, multiplexer_32_out;

  Choose choose_1 (
    .in_1(1'b1), .in_2(A1), .out_3(choose_1_out_3), .out_4(choose_1_out_4), .out_5(choose_1_out_5),
    .out_6(choose_1_out_6), .out_7(choose_1_out_7), .out_8(choose_1_out_8), .out_9(choose_1_out_9),
    .out_10(choose_1_out_10), .out_11(choose_1_out_11), .out_12(choose_1_out_12), .out_13(choose_1_out_13),
    .out_14(choose_1_out_14), .out_15(choose_1_out_15), .out_16(choose_1_out_16), .out_17(choose_1_out_17),
    .out_18(choose_1_out_18), .out_19(choose_1_out_19), .out_20(choose_1_out_20), .out_21(choose_1_out_21),
    .out_22(choose_1_out_22), .out_23(choose_1_out_23), .out_24(choose_1_out_24), .out_25(choose_1_out_25),
    .out_26(choose_1_out_26), .out_27(choose_1_out_27), .out_28(choose_1_out_28), .out_29(choose_1_out_29),
    .out_30(choose_1_out_30), .out_31(choose_1_out_31), .out_32(choose_1_out_32), .out_33(choose_1_out_33),
    .out_34(choose_1_out_34));
  Multiplexer #(.width(32)) multiplexer_1 (
    .in0({32{1'b0}}), .in1(in_2), .out(multiplexer_1_out), .sel(choose_1_out_3), .en(1'b1));
  Multiplexer #(.width(32)) multiplexer_2 (
    .in0({32{1'b0}}), .in1(in_3), .out(multiplexer_2_out), .sel(choose_1_out_4), .en(1'b1));
  Multiplexer #(.width(32)) multiplexer_3 (
    .in0({32{1'b0}}), .in1(in_4), .out(multiplexer_3_out), .sel(choose_1_out_5), .en(1'b1));
  Multiplexer #(.width(32)) multiplexer_4 (
    .in0({32{1'b0}}), .in1(in_5), .out(multiplexer_4_out), .sel(choose_1_out_6), .en(1'b1));
  Multiplexer #(.width(32)) multiplexer_5 (
    .in0({32{1'b0}}), .in1(in_6), .out(multiplexer_5_out), .sel(choose_1_out_7), .en(1'b1));
  Multiplexer #(.width(32)) multiplexer_6 (
    .in0({32{1'b0}}), .in1(in_7), .out(multiplexer_6_out), .sel(choose_1_out_8), .en(1'b1));
  Multiplexer #(.width(32)) multiplexer_7 (
    .in0({32{1'b0}}), .in1(in_8), .out(multiplexer_7_out), .sel(choose_1_out_9), .en(1'b1));
  Multiplexer #(.width(32)) multiplexer_8 (
    .in0({32{1'b0}}), .in1(in_9), .out(multiplexer_8_out), .sel(choose_1_out_10), .en(1'b1));
  Multiplexer #(.width(32)) multiplexer_9 (
    .in0({32{1'b0}}), .in1(in_10), .out(multiplexer_9_out), .sel(choose_1_out_11), .en(1'b1));
  Multiplexer #(.width(32)) multiplexer_10 (
    .in0({32{1'b0}}), .in1(in_11), .out(multiplexer_10_out), .sel(choose_1_out_12), .en(1'b1));
  Multiplexer #(.width(32)) multiplexer_11 (
    .in0({32{1'b0}}), .in1(in_12), .out(multiplexer_11_out), .sel(choose_1_out_13), .en(1'b1));
  Multiplexer #(.width(32)) multiplexer_12 (
    .in0({32{1'b0}}), .in1(in_13), .out(multiplexer_12_out), .sel(choose_1_out_14), .en(1'b1));
  Multiplexer #(.width(32)) multiplexer_13 (
    .in0({32{1'b0}}), .in1(in_14), .out(multiplexer_13_out), .sel(choose_1_out_15), .en(1'b1));
  Multiplexer #(.width(32)) multiplexer_14 (
    .in0({32{1'b0}}), .in1(in_15), .out(multiplexer_14_out), .sel(choose_1_out_16), .en(1'b1));
  Multiplexer #(.width(32)) multiplexer_15 (
    .in0({32{1'b0}}), .in1(in_16), .out(multiplexer_15_out), .sel(choose_1_out_17), .en(1'b1));
  Multiplexer #(.width(32)) multiplexer_16 (
    .in0({32{1'b0}}), .in1(in_17), .out(multiplexer_16_out), .sel(choose_1_out_18), .en(1'b1));
  Multiplexer #(.width(32)) multiplexer_17 (
    .in0({32{1'b0}}), .in1(in_18), .out(multiplexer_17_out), .sel(choose_1_out_19), .en(1'b1));
  Multiplexer #(.width(32)) multiplexer_18 (
    .in0({32{1'b0}}), .in1(in_19), .out(multiplexer_18_out), .sel(choose_1_out_20), .en(1'b1));
  Multiplexer #(.width(32)) multiplexer_19 (
    .in0({32{1'b0}}), .in1(in_20), .out(multiplexer_19_out), .sel(choose_1_out_21), .en(1'b1));
  Multiplexer #(.width(32)) multiplexer_20 (
    .in0({32{1'b0}}), .in1(in_21), .out(multiplexer_20_out), .sel(choose_1_out_22), .en(1'b1));
  Multiplexer #(.width(32)) multiplexer_21 (
    .in0({32{1'b0}}), .in1(in_22), .out(multiplexer_21_out), .sel(choose_1_out_23), .en(1'b1));
  Multiplexer #(.width(32)) multiplexer_22 (
    .in0({32{1'b0}}), .in1(in_23), .out(multiplexer_22_out), .sel(choose_1_out_24), .en(1'b1));
  Multiplexer #(.width(32)) multiplexer_23 (
    .in0({32{1'b0}}), .in1(in_24), .out(multiplexer_23_out), .sel(choose_1_out_25), .en(1'b1));
  Multiplexer #(.width(32)) multiplexer_24 (
    .in0({32{1'b0}}), .in1(in_25), .out(multiplexer_24_out), .sel(choose_1_out_26), .en(1'b1));
  Multiplexer #(.width(32)) multiplexer_25 (
    .in0({32{1'b0}}), .in1(in_26), .out(multiplexer_25_out), .sel(choose_1_out_27), .en(1'b1));
  Multiplexer #(.width(32)) multiplexer_26 (
    .in0({32{1'b0}}), .in1(in_27), .out(multiplexer_26_out), .sel(choose_1_out_28), .en(1'b1));
  Multiplexer #(.width(32)) multiplexer_27 (
    .in0({32{1'b0}}), .in1(in_28), .out(multiplexer_27_out), .sel(choose_1_out_29), .en(1'b1));
  Multiplexer #(.width(32)) multiplexer_28 (
    .in0({32{1'b0}}), .in1(in_29), .out(multiplexer_28_out), .sel(choose_1_out_30), .en(1'b1));
  Multiplexer #(.width(32)) multiplexer_29 (
    .in0({32{1'b0}}), .in1(in_30), .out(multiplexer_29_out), .sel(choose_1_out_31), .en(1'b1));
  Multiplexer #(.width(32)) multiplexer_30 (
    .in0({32{1'b0}}), .in1(in_31), .out(multiplexer_30_out), .sel(choose_1_out_32), .en(1'b1));
  Multiplexer #(.width(32)) multiplexer_31 (
    .in0({32{1'b0}}), .in1(in_32), .out(multiplexer_31_out), .sel(choose_1_out_33), .en(1'b1));
  Multiplexer #(.width(32)) multiplexer_32 (
    .in0({32{1'b0}}), .in1(in_33), .out(multiplexer_32_out), .sel(choose_1_out_34), .en(1'b1));
  assign out_34 = multiplexer_1_out | multiplexer_2_out | multiplexer_3_out | multiplexer_4_out | multiplexer_5_out | multiplexer_6_out | multiplexer_7_out | multiplexer_8_out | multiplexer_9_out | multiplexer_10_out | multiplexer_11_out | multiplexer_12_out | multiplexer_13_out | multiplexer_14_out | multiplexer_15_out | multiplexer_16_out | multiplexer_17_out | multiplexer_18_out | multiplexer_19_out | multiplexer_20_out | multiplexer_21_out | multiplexer_22_out | multiplexer_23_out | multiplexer_24_out | multiplexer_25_out | multiplexer_26_out | multiplexer_27_out | multiplexer_28_out | multiplexer_29_out | multiplexer_30_out | multiplexer_31_out | multiplexer_32_out;  // OR_Gate or_1, 32 bits wide
endmodule

// GRF
module grf (
  input  Clk,
  input  Enabled,
  input  reset,
  input  [4:0] A1,
  input  [4:0] A2,
  input  [4:0] A3,
  input  [31:0] WD3,
  output [31:0] RD1,
  output [31:0] RD2
);

  wire _0, _1, _2, _3, _4, _5, _6, _7, _8, _9, _10, _11, _12, _13, _14, _15, _16, _17, _18, _19, _20, _21,
       _22, _23, _24, _25, _26, _27, _28, _29, _30, _31;
  wire [31:0] multiplexer_1_out, multiplexer_2_out, multiplexer_3_out, multiplexer_4_out, multiplexer_5_out,
       multiplexer_6_out, multiplexer_7_out, multiplexer_8_out, multiplexer_9_out, multiplexer_10_out,
       multiplexer_11_out, multiplexer_12_out, multiplexer_13_out, multiplexer_14_out, multiplexer_15_out,
       multiplexer_16_out, multiplexer_17_out, multiplexer_18_out, multiplexer_19_out, multiplexer_20_out,
       multiplexer_21_out, multiplexer_22_out, multiplexer_23_out, multiplexer_24_out, multiplexer_25_out,
       multiplexer_26_out, multiplexer_27_out, multiplexer_28_out, multiplexer_29_out, multiplexer_30_out,
       multiplexer_31_out, multiplexer_32_out, Out_0, Out_1, Out_2, Out_3, Out_4, Out_5, Out_6, Out_7, Out_8,
       Out_9, Out_10, Out_11, Out_12, Out_13, Out_14, Out_15, Out_16, Out_17, Out_18, Out_19, Out_20, Out_21,
       Out_22, Out_23, Out_24, Out_25, Out_26, Out_27, Out_28, Out_29, Out_30, Out_31, register_1_q;

  Choose choose_1 (
    .in_1(1'b1), .in_2(A3), .out_3(_0), .out_4(_1), .out_5(_2), .out_6(_3), .out_7(_4), .out_8(_5),
    .out_9(_6), .out_10(_7), .out_11(_8), .out_12(_9), .out_13(_10), .out_14(_11), .out_15(_12),
    .out_16(_13), .out_17(_14), .out_18(_15), .out_19(_16), .out_20(_17), .out_21(_18), .out_22(_19),
    .out_23(_20), .out_24(_21), .out_25(_22), .out_26(_23), .out_27(_24), .out_28(_25), .out_29(_26),
    .out_30(_27), .out_31(_28), .out_32(_29), .out_33(_30), .out_34(_31));
  choose_output choose_output_1 (
    .A1(A1), .in_2(Out_0), .in_3(Out_1), .in_4(Out_2), .in_5(Out_3), .in_6(Out_4), .in_7(Out_5),
    .in_8(Out_6), .in_9(Out_7), .in_10(Out_8), .in_11(Out_9), .in_12(Out_10), .in_13(Out_11), .in_14(Out_12),
    .in_15(Out_13), .in_16(Out_14), .in_17(Out_15), .in_18(Out_16), .in_19(Out_17), .in_20(Out_18),
    .in_21(Out_19), .in_22(Out_20), .in_23(Out_21), .in_24(Out_22), .in_25(Out_23), .in_26(Out_24),
    .in_27(Out_25), .in_28(Out_26), .in_29(Out_27), .in_30(Out_28), .in_31(Out_29), .in_32(Out_30),
    .in_33(Out_31), .out_34(RD1));
  choose_output choose_output_2 (
    .A1(A2), .in_2(Out_0), .in_3(Out_1), .in_4(Out_2), .in_5(Out_3), .in_6(Out_4), .in_7(Out_5),
    .in_8(Out_6), .in_9(Out_7), .in_10(Out_8), .in_11(Out_9), .in_12(Out_10), .in_13(Out_11), .in_14(Out_12),
    .in_15(Out_13), .in_16(Out_14), .in_17(Out_15), .in_18(Out_16), .in_19(Out_17), .in_20(Out_18),
    .in_21(Out_19), .in_22(Out_20), .in_23(Out_21), .in_24(Out_22), .in_25(Out_23), .in_26(Out_24),
    .in_27(Out_25), .in_28(Out_26), .in_29(Out_27), .in_30(Out_28), .in_31(Out_29), .in_32(Out_30),
    .in_33(Out_31), .out_34(RD2));
  Multiplexer #(.width(32)) multiplexer_1 (.in0(register_1_q), .in1(WD3), .out(multiplexer_1_out), .sel(_0), .en(1'b1));
  Multiplexer #(.width(32)) multiplexer_2 (.in0(Out_1), .in1(WD3), .out(multiplexer_2_out), .sel(_1), .en(1'b1));
  Multiplexer #(.width(32)) multiplexer_3 (.in0(Out_2), .in1(WD3), .out(multiplexer_3_out), .sel(_2), .en(1'b1));
  Multiplexer #(.width(32)) multiplexer_4 (.in0(Out_3), .in1(WD3), .out(multiplexer_4_out), .sel(_3), .en(1'b1));
  Multiplexer #(.width(32)) multiplexer_5 (.in0(Out_4), .in1(WD3), .out(multiplexer_5_out), .sel(_4), .en(1'b1));
  Multiplexer #(.width(32)) multiplexer_6 (.in0(Out_5), .in1(WD3), .out(multiplexer_6_out), .sel(_5), .en(1'b1));
  Multiplexer #(.width(32)) multiplexer_7 (.in0(Out_6), .in1(WD3), .out(multiplexer_7_out), .sel(_6), .en(1'b1));
  Multiplexer #(.width(32)) multiplexer_8 (.in0(Out_7), .in1(WD3), .out(multiplexer_8_out), .sel(_7), .en(1'b1));
  Multiplexer #(.width(32)) multiplexer_9 (.in0(Out_8), .in1(WD3), .out(multiplexer_9_out), .sel(_8), .en(1'b1));
  Multiplexer #(.width(32)) multiplexer_10 (.in0(Out_9), .in1(WD3), .out(multiplexer_10_out), .sel(_9), .en(1'b1));
  Multiplexer #(.width(32)) multiplexer_11 (.in0(Out_10), .in1(WD3), .out(multiplexer_11_out), .sel(_10), .en(1'b1));
  Multiplexer #(.width(32)) multiplexer_12 (.in0(Out_11), .in1(WD3), .out(multiplexer_12_out), .sel(_11), .en(1'b1));
  Multiplexer #(.width(32)) multiplexer_13 (.in0(Out_12), .in1(WD3), .out(multiplexer_13_out), .sel(_12), .en(1'b1));
  Multiplexer #(.width(32)) multiplexer_14 (.in0(Out_13), .in1(WD3), .out(multiplexer_14_out), .sel(_13), .en(1'b1));
  Multiplexer #(.width(32)) multiplexer_15 (.in0(Out_14), .in1(WD3), .out(multiplexer_15_out), .sel(_14), .en(1'b1));
  Multiplexer #(.width(32)) multiplexer_16 (.in0(Out_15), .in1(WD3), .out(multiplexer_16_out), .sel(_15), .en(1'b1));
  Register #(.width(32)) register_1 (.D(multiplexer_1_out), .en(Enabled), .Q(register_1_q), .clk(Clk), .clr(reset));
  Register #(.width(32)) register_2 (.D(multiplexer_2_out), .en(Enabled), .Q(Out_1), .clk(Clk), .clr(reset));
  Register #(.width(32)) register_3 (.D(multiplexer_3_out), .en(Enabled), .Q(Out_2), .clk(Clk), .clr(reset));
  Register #(.width(32)) register_4 (.D(multiplexer_4_out), .en(Enabled), .Q(Out_3), .clk(Clk), .clr(reset));
  Register #(.width(32)) register_5 (.D(multiplexer_5_out), .en(Enabled), .Q(Out_4), .clk(Clk), .clr(reset));
  Register #(.width(32)) register_6 (.D(multiplexer_6_out), .en(Enabled), .Q(Out_5), .clk(Clk), .clr(reset));
  Register #(.width(32)) register_7 (.D(multiplexer_7_out), .en(Enabled), .Q(Out_6), .clk(Clk), .clr(reset));
  Register #(.width(32)) register_8 (.D(multiplexer_8_out), .en(Enabled), .Q(Out_7), .clk(Clk), .clr(reset));
  Register #(.width(32)) register_9 (.D(multiplexer_9_out), .en(Enabled), .Q(Out_8), .clk(Clk), .clr(reset));
  Register #(.width(32)) register_10 (.D(multiplexer_10_out), .en(Enabled), .Q(Out_9), .clk(Clk), .clr(reset));
  Register #(.width(32)) register_11 (.D(multiplexer_11_out), .en(Enabled), .Q(Out_10), .clk(Clk), .clr(reset));
  Register #(.width(32)) register_12 (.D(multiplexer_12_out), .en(Enabled), .Q(Out_11), .clk(Clk), .clr(reset));
  Register #(.width(32)) register_13 (.D(multiplexer_13_out), .en(Enabled), .Q(Out_12), .clk(Clk), .clr(reset));
  Register #(.width(32)) register_14 (.D(multiplexer_14_out), .en(Enabled), .Q(Out_13), .clk(Clk), .clr(reset));
  Register #(.width(32)) register_15 (.D(multiplexer_15_out), .en(Enabled), .Q(Out_14), .clk(Clk), .clr(reset));
  Register #(.width(32)) register_16 (.D(multiplexer_16_out), .en(Enabled), .Q(Out_15), .clk(Clk), .clr(reset));
  assign Out_0 = {32{1'b0}} & register_1_q;  // AND_Gate and_1, 32 bits wide
  Multiplexer #(.width(32)) multiplexer_17 (.in0(Out_16), .in1(WD3), .out(multiplexer_17_out), .sel(_16), .en(1'b1));
  Multiplexer #(.width(32)) multiplexer_18 (.in0(Out_17), .in1(WD3), .out(multiplexer_18_out), .sel(_17), .en(1'b1));
  Multiplexer #(.width(32)) multiplexer_19 (.in0(Out_18), .in1(WD3), .out(multiplexer_19_out), .sel(_18), .en(1'b1));
  Multiplexer #(.width(32)) multiplexer_20 (.in0(Out_19), .in1(WD3), .out(multiplexer_20_out), .sel(_19), .en(1'b1));
  Multiplexer #(.width(32)) multiplexer_21 (.in0(Out_20), .in1(WD3), .out(multiplexer_21_out), .sel(_20), .en(1'b1));
  Multiplexer #(.width(32)) multiplexer_22 (.in0(Out_21), .in1(WD3), .out(multiplexer_22_out), .sel(_21), .en(1'b1));
  Multiplexer #(.width(32)) multiplexer_23 (.in0(Out_22), .in1(WD3), .out(multiplexer_23_out), .sel(_22), .en(1'b1));
  Multiplexer #(.width(32)) multiplexer_24 (.in0(Out_23), .in1(WD3), .out(multiplexer_24_out), .sel(_23), .en(1'b1));
  Multiplexer #(.width(32)) multiplexer_25 (.in0(Out_24), .in1(WD3), .out(multiplexer_25_out), .sel(_24), .en(1'b1));
  Multiplexer #(.width(32)) multiplexer_26 (.in0(Out_25), .in1(WD3), .out(multiplexer_26_out), .sel(_25), .en(1'b1));
  Multiplexer #(.width(32)) multiplexer_27 (.in0(Out_26), .in1(WD3), .out(multiplexer_27_out), .sel(_26), .en(1'b1));
  Multiplexer #(.width(32)) multiplexer_28 (.in0(Out_27), .in1(WD3), .out(multiplexer_28_out), .sel(_27), .en(1'b1));
  Multiplexer #(.width(32)) multiplexer_29 (.in0(Out_28), .in1(WD3), .out(multiplexer_29_out), .sel(_28), .en(1'b1));
  Multiplexer #(.width(32)) multiplexer_30 (.in0(Out_29), .in1(WD3), .out(multiplexer_30_out), .sel(_29), .en(1'b1));
  Multiplexer #(.width(32)) multiplexer_31 (.in0(Out_30), .in1(WD3), .out(multiplexer_31_out), .sel(_30), .en(1'b1));
  Multiplexer #(.width(32)) multiplexer_32 (.in0(Out_31), .in1(WD3), .out(multiplexer_32_out), .sel(_31), .en(1'b1));
  Register #(.width(32)) register_17 (.D(multiplexer_17_out), .en(Enabled), .Q(Out_16), .clk(Clk), .clr(reset));
  Register #(.width(32)) register_18 (.D(multiplexer_18_out), .en(Enabled), .Q(Out_17), .clk(Clk), .clr(reset));
  Register #(.width(32)) register_19 (.D(multiplexer_19_out), .en(Enabled), .Q(Out_18), .clk(Clk), .clr(reset));
  Register #(.width(32)) register_20 (.D(multiplexer_20_out), .en(Enabled), .Q(Out_19), .clk(Clk), .clr(reset));
  Register #(.width(32)) register_21 (.D(multiplexer_21_out), .en(Enabled), .Q(Out_20), .clk(Clk), .clr(reset));
  Register #(.width(32)) register_22 (.D(multiplexer_22_out), .en(Enabled), .Q(Out_21), .clk(Clk), .clr(reset));
  Register #(.width(32)) register_23 (.D(multiplexer_23_out), .en(Enabled), .Q(Out_22), .clk(Clk), .clr(reset));
  Register #(.width(32)) register_24 (.D(multiplexer_24_out), .en(Enabled), .Q(Out_23), .clk(Clk), .clr(reset));
  Register #(.width(32)) register_25 (.D(multiplexer_25_out), .en(Enabled), .Q(Out_24), .clk(Clk), .clr(reset));
  Register #(.width(32)) register_26 (.D(multiplexer_26_out), .en(Enabled), .Q(Out_25), .clk(Clk), .clr(reset));
  Register #(.width(32)) register_27 (.D(multiplexer_27_out), .en(Enabled), .Q(Out_26), .clk(Clk), .clr(reset));
  Register #(.width(32)) register_28 (.D(multiplexer_28_out), .en(Enabled), .Q(Out_27), .clk(Clk), .clr(reset));
  Register #(.width(32)) register_29 (.D(multiplexer_29_out), .en(Enabled), .Q(Out_28), .clk(Clk), .clr(reset));
  Register #(.width(32)) register_30 (.D(multiplexer_30_out), .en(Enabled), .Q(Out_29), .clk(Clk), .clr(reset));
  Register #(.width(32)) register_31 (.D(multiplexer_31_out), .en(Enabled), .Q(Out_30), .clk(Clk), .clr(reset));
  Register #(.width(32)) register_32 (.D(multiplexer_32_out), .en(Enabled), .Q(Out_31), .clk(Clk), .clr(reset));

  // Other names for the same wires on the sheet: Input_number[31:0] = WD3; WD[31:0] = WD3
endmodule

module ALU (
  input  [2:0] ALUOp,
  input  [31:0] SrcA,
  input  [31:0] SrcB,
  output [31:0] ALUResult,
  output ZERO
);

  wire comparator_1_eq, comparator_2_eq, comparator_3_eq, comparator_4_eq, comparator_5_eq, comparator_6_eq;
  wire [31:0] adder_1_out, and_1_out, bit_extender_1_out, multiplexer_1_out, multiplexer_2_out,
       multiplexer_3_out, multiplexer_4_out, multiplexer_5_out, or_1_out, subtractor_1_out;

  Comparator #(.width(3), .mode("unsigned")) comparator_1 (
    .a(3'b010), .b(ALUOp), .eq(comparator_1_eq));  // open: gt, lt
  Comparator #(.width(3), .mode("unsigned")) comparator_2 (
    .a(3'b110), .b(ALUOp), .eq(comparator_2_eq));  // open: gt, lt
  Adder #(.width(32)) adder_1 (.a(SrcA), .b(SrcB), .out(adder_1_out));  // open: cin, cout
  Subtractor #(.width(32)) subtractor_1 (.a(SrcA), .b(SrcB), .out(subtractor_1_out));  // open: bin, bout
  assign or_1_out = SrcA | SrcB;  // OR_Gate or_1, 32 bits wide
  assign and_1_out = SrcA & SrcB;  // AND_Gate and_1, 32 bits wide
  Comparator #(.width(32)) comparator_3 (.a(SrcB), .b(SrcA), .eq(comparator_3_eq));  // open: gt, lt
  assign bit_extender_1_out = {{31{1'b0}}, comparator_3_eq};  // Bit_Extender bit_extender_1
  Comparator #(.width(3), .mode("unsigned")) comparator_4 (
    .a(3'b000), .b(ALUOp), .eq(comparator_4_eq));  // open: gt, lt
  Comparator #(.width(3), .mode("unsigned")) comparator_5 (
    .a(3'b001), .b(ALUOp), .eq(comparator_5_eq));  // open: gt, lt
  Comparator #(.width(3), .mode("unsigned")) comparator_6 (
    .a(3'b111), .b(ALUOp), .eq(comparator_6_eq));  // open: gt, lt
  Multiplexer #(.width(32)) multiplexer_1 (
    .in0({32{1'b0}}), .in1(adder_1_out), .out(multiplexer_1_out), .sel(comparator_1_eq), .en(1'b1));
  Multiplexer #(.width(32)) multiplexer_2 (
    .in0({32{1'b0}}), .in1(subtractor_1_out), .out(multiplexer_2_out), .sel(comparator_2_eq), .en(1'b1));
  Multiplexer #(.width(32)) multiplexer_3 (
    .in0({32{1'b0}}), .in1(or_1_out), .out(multiplexer_3_out), .sel(comparator_5_eq), .en(1'b1));
  Multiplexer #(.width(32)) multiplexer_4 (
    .in0({32{1'b0}}), .in1(and_1_out), .out(multiplexer_4_out), .sel(comparator_4_eq), .en(1'b1));
  Multiplexer #(.width(32)) multiplexer_5 (
    .in0({32{1'b0}}), .in1(bit_extender_1_out), .out(multiplexer_5_out), .sel(comparator_6_eq), .en(1'b1));
  assign ALUResult = multiplexer_1_out | multiplexer_2_out | multiplexer_3_out | multiplexer_4_out | multiplexer_5_out;  // OR_Gate or_2, 32 bits wide
  Comparator #(.width(32), .mode("unsigned")) comparator_7 (.a({32{1'b0}}), .b(ALUResult), .eq(ZERO));  // open: gt, lt
endmodule

module control (
  input  A,
  input  B,
  input  C,
  input  D,
  input  Extra1,
  input  Extra2,
  output RegDst,
  output WE3,
  output WE,
  output ALUcontrol_1,
  output ALUcontrol_2,
  output ALUcontrol_3,
  output MemtoRReg,
  output ALUSrc,
  output ALUSrc2,
  output Branch
);

  wire and_2_out, and_3_out, and_5_out, and_6_out, and_9_out, and_10_out, not_1_out, not_2_out, not_3_out,
       not_4_out, not_5_out, not_6_out, not_7_out, not_8_out, not_9_out;

  not not_1 (not_1_out, A);
  not not_2 (not_2_out, B);
  not not_3 (not_3_out, D);
  not not_4 (not_4_out, D);
  not not_5 (not_5_out, C);
  not not_6 (not_6_out, A);
  and and_1 (ALUSrc, A, B);
  not not_7 (not_7_out, B);
  not not_8 (not_8_out, C);
  not not_9 (not_9_out, D);
  and and_2 (and_2_out, not_1_out, C);
  and and_3 (and_3_out, A, B);
  and and_4 (WE, A, not_2_out);
  and and_5 (and_5_out, B, not_3_out);
  and and_6 (and_6_out, B, not_4_out);
  and and_7 (ALUcontrol_3, B, not_5_out);
  and and_8 (MemtoRReg, not_6_out, D);
  and and_9 (and_9_out, not_7_out, D);
  and and_10 (and_10_out, A, not_8_out);
  and and_11 (Branch, B, not_9_out);
  or or_1 (WE3, Extra1, and_2_out, and_3_out);
  or or_2 (ALUcontrol_1, Extra2, and_5_out);
  or or_3 (ALUcontrol_2, Extra1, C, and_6_out);
  or or_4 (ALUSrc2, and_9_out, and_10_out);

  assign RegDst = Extra1;
endmodule

module main (
  input  in_1,
  output [31:0] Instr,
  output RegWrite,
  output [4:0] RegAddr,
  output [31:0] RegData,
  output MemWrite,
  output [4:0] MemAddr,
  output [31:0] MemData
);

  wire and_1_out, Branch, clk, comparator_1_eq, Equal, MemtoReg, not_1_out, not_2_out, RegDst;
  wire [1:0] ALUSrc, multiplexer_3_out;
  wire [2:0] ALUControl;
  wire [4:0] multiplexer_2_out, Next_instr, Next_instr_add_imme, PC_q;
  wire [31:0] alu_1_aluresult, bit_extender_1_out, ext_1_signext, ext_1_srcb, grf_1_rd1, ram_1_data;
  wire [31:5] adder_2_out;

  Clock clock_1 (.out(clk));
  Multiplexer #(.width(5)) multiplexer_1 (
    .in0(Instr[20:16]), .in1(Instr[15:11]), .out(RegAddr), .sel(RegDst), .en(1'b1));
  not not_1 (not_1_out, Equal);
  and and_1 (and_1_out, Branch, not_1_out);
  grf grf_1 (
    .A1(Instr[25:21]), .A2(Instr[20:16]), .A3(RegAddr), .WD3(RegData), .RD1(grf_1_rd1), .RD2(MemData),
    .reset(in_1), .Clk(clk), .Enabled(RegWrite));
  Multiplexer #(.width(5)) multiplexer_2 (
    .in0(Next_instr), .in1(Next_instr_add_imme), .out(multiplexer_2_out), .sel(and_1_out), .en(1'b1));
  Register #(.width(5)) PC (.D(multiplexer_2_out), .en(1'b1), .Q(PC_q), .clk(clk), .clr(in_1));
  Comparator #(.width(6), .mode("unsigned")) comparator_1 (
    .a(Instr[31:26]), .b({6{1'b0}}), .eq(comparator_1_eq));  // open: gt, lt
  Multiplexer #(.width(2)) multiplexer_3 (
    .in0(2'b00), .in1({Instr[5], Instr[1]}), .out(multiplexer_3_out), .sel(comparator_1_eq), .en(1'b1));
  Adder #(.width(5)) adder_1 (.a(PC_q), .b(5'b00001), .out(Next_instr));  // open: cin, cout
  EXT ext_1 (.RD2(MemData), .ALUSrc(ALUSrc), .Immediate1(Instr[15:0]), .SrcB(ext_1_srcb), .SignEXT(ext_1_signext));
  ROM #(.addrWidth(5), .dataWidth(32)) rom_1 (.addr(PC_q), .data(Instr));  // open: sel
  ALU alu_1 (
    .SrcA(grf_1_rd1), .ALUResult({alu_1_aluresult[31:7], MemAddr, alu_1_aluresult[1:0]}), .ALUOp(ALUControl),
    .ZERO(Equal), .SrcB(ext_1_srcb));
  control control_1 (
    .A(Instr[29]), .B(Instr[28]), .C(Instr[27]), .D(Instr[26]), .Extra1(multiplexer_3_out[1]),
    .Extra2(multiplexer_3_out[0]), .RegDst(RegDst), .WE3(RegWrite), .WE(MemWrite),
    .ALUcontrol_1(ALUControl[2]), .ALUcontrol_2(ALUControl[1]), .ALUcontrol_3(ALUControl[0]),
    .MemtoRReg(MemtoReg), .ALUSrc(ALUSrc[1]), .ALUSrc2(ALUSrc[0]), .Branch(Branch));
  assign bit_extender_1_out = {{27{1'b0}}, Next_instr};  // Bit_Extender bit_extender_1
  Adder #(.width(32)) adder_2 (
    .a(ext_1_signext), .b(bit_extender_1_out), .out({adder_2_out, Next_instr_add_imme}));  // open: cin, cout
  RAM #(.addrWidth(5), .dataWidth(32), .bus("separate")) ram_1 (
    .addr(MemAddr), .din(MemData), .data(ram_1_data), .str(MemWrite), .clk(clk), .ld(not_2_out), .clr(in_1));  // open: sel
  not not_2 (not_2_out, MemWrite);
  Multiplexer #(.width(32)) multiplexer_4 (
    .in0({alu_1_aluresult[31:7], MemAddr, alu_1_aluresult[1:0]}), .in1(ram_1_data), .out(RegData),
    .sel(MemtoReg), .en(1'b1));

  // Other names for the same wires on the sheet: Function[5:0] = Instr[5:0]; Immediate1[15:0] = Instr[15:0];
  //   _0[4:0] = Instr[10:6]; rd[4:0] = Instr[15:11]; reset = in_1; rs_base[4:0] = Instr[25:21];
  //   rt[4:0] = Instr[20:16]; Special[5:0] = Instr[31:26]; WE = MemWrite; WE3 = RegWrite

  // Notes on the sheet:
  //   contents of rom_1 (hex, n*v repeats v):
  //   34013456 34221879 411021 10220008 34030009 ac620007 34020011 34010001 411023 3c081234 ac480004
  //   8c490000 220823 ac41fffc 8c55fffc 481021 3c111be2 511021 0 340f0001 22f8823 1220fffd ac030008
endmodule

module EXT (
  input  [31:0] RD2,
  input  [1:0] ALUSrc,
  input  [15:0] Immediate1,
  output [31:0] SrcB,
  output [31:0] SignEXT
);

  wire [31:0] bit_extender_2_out;

  assign SignEXT = {{16{Immediate1[15]}}, Immediate1};  // Bit_Extender bit_extender_1
  assign bit_extender_2_out = {{16{1'b0}}, Immediate1};  // Bit_Extender bit_extender_2
  Multiplexer #(.select(2), .width(32)) multiplexer_1 (
    .in0(RD2), .in1(SignEXT), .in2({Immediate1, {16{1'b0}}}), .in3(bit_extender_2_out), .out(SrcB),
    .sel(ALUSrc), .en(1'b1));
endmodule
