// Logisim project TEST1.circ as structural Verilog
module SSS (
  input  A,
  input  B,
  input  C,
  input  in_4,
  input  in_5,
  input  in_6,
  output Y,
  output out_8,
  output out_9
);

  wire and_1_out, and_2_out, and_3_out, and_4_out, and_5_out, and_6_out, not_1_out, not_2_out, not_3_out;

  not not_1 (not_1_out, C);
  and and_1 (and_1_out, B, C);
  and and_2 (and_2_out, A, not_1_out);
  not not_2 (not_2_out, in_6);
  not not_3 (not_3_out, in_6);
  or or_1 (Y, and_1_out, and_2_out);
  and and_3 (and_3_out, in_5, in_6);
  and and_4 (and_4_out, in_4, not_2_out);
  and and_5 (and_5_out, in_5, not_3_out);
  and and_6 (and_6_out, in_4, in_6);
  or or_2 (out_8, and_3_out, and_4_out);
  or or_3 (out_9, and_5_out, and_6_out);
endmodule

module SSSS (
  input  A,
  input  B,
  input  C,
  output Y
);

  wire nand_1_out, nand_2_out, nand_3_out;

  nand nand_1 (nand_1_out, C, C);
  nand nand_2 (nand_2_out, B, C);
  nand nand_3 (nand_3_out, A, nand_1_out);
  nand nand_4 (Y, nand_2_out, nand_3_out);
endmodule
