// Logisim project alu.circ as structural Verilog
module alu (
  input  [3:0] A,
  input  [3:0] B,
  input  [1:0] ALUOp,
  output [3:0] C
);

  wire [3:0] adder_1_out, and_1_out, and_2_out, and_3_out, and_4_out, and_5_out, or_1_out, subtractor_1_out;
  wire [3:3] comparator_1_eq, comparator_2_eq, comparator_3_eq, comparator_4_eq;

  assign and_1_out = A & B;  // AND_Gate and_1, 4 bits wide
  assign or_1_out = A | B;  // OR_Gate or_1, 4 bits wide
  Adder #(.width(4)) adder_1 (.a(A), .b(B), .out(adder_1_out));  // open: cin, cout
  Comparator #(.width(2), .mode("unsigned")) comparator_1 (
    .a(ALUOp), .b(2'b00), .eq(comparator_1_eq[3]));  // open: gt, lt
  Comparator #(.width(2), .mode("unsigned")) comparator_2 (
    .a(ALUOp), .b(2'b01), .eq(comparator_2_eq[3]));  // open: gt, lt
  Subtractor #(.width(4)) subtractor_1 (.a(A), .b(B), .out(subtractor_1_out));  // open: bin, bout
  Comparator #(.width(2), .mode("unsigned")) comparator_3 (
    .a(ALUOp), .b(2'b10), .eq(comparator_3_eq[3]));  // open: gt, lt
  Comparator #(.width(2), .mode("unsigned")) comparator_4 (
    .a(ALUOp), .b(2'b11), .eq(comparator_4_eq[3]));  // open: gt, lt
  assign and_2_out = {4{comparator_3_eq[3]}} & and_1_out;  // AND_Gate and_2, 4 bits wide
  assign and_3_out = {4{comparator_4_eq[3]}} & or_1_out;  // AND_Gate and_3, 4 bits wide
  assign and_4_out = adder_1_out & {4{comparator_1_eq[3]}};  // AND_Gate and_4, 4 bits wide
  assign and_5_out = {4{comparator_2_eq[3]}} & subtractor_1_out;  // AND_Gate and_5, 4 bits wide
  assign C = and_4_out | and_5_out | and_2_out | and_3_out;  // OR_Gate or_2, 4 bits wide
endmodule
