// Logisim project fsm.circ as structural Verilog
module fsm (
  input  in_1,
  input  [1:0] in_2,
  output out_3
);

  wire clock_1_out, comparator_1_eq, register_1_q;
  wire [2:0] next_1_n3, next_2_n3, register_2_q;

  Next next_1 (
    .In1(in_2[1]), .In2(in_2[0]), .A1(register_2_q[2]), .A2(register_2_q[1]), .A3(register_2_q[0]),
    .N1(next_1_n3[2]), .N2(next_1_n3[1]), .N3(next_1_n3[0]));
  Clock clock_1 (.out(clock_1_out));
  Register #(.width(1)) register_1 (.D(in_1), .Q(register_1_q), .clk(clock_1_out), .clr(register_1_q));  // open: en
  Register #(.width(3)) register_2 (
    .D(next_1_n3), .Q(register_2_q), .clk(clock_1_out), .clr(register_1_q));  // open: en
  Next next_2 (
    .In1(in_2[1]), .In2(in_2[0]), .A1(register_2_q[2]), .A2(register_2_q[1]), .A3(register_2_q[0]),
    .N1(next_2_n3[2]), .N2(next_2_n3[1]), .N3(next_2_n3[0]));
  Comparator #(.width(3), .mode("unsigned")) comparator_1 (
    .a(next_2_n3), .b(3'b100), .eq(comparator_1_eq));  // open: gt, lt
  and and_1 (out_3, comparator_1_eq, 1'b1);
endmodule

module Next (
  input  In1,
  input  In2,
  input  A1,
  input  A2,
  input  A3,
  output N1,
  output N2,
  output N3
);

  wire and_3_out, and_4_out, and_5_out, not_1_out, not_2_out, not_3_out, not_4_out, not_5_out, not_6_out,
       not_7_out, not_8_out, not_9_out, not_10_out, not_11_out, not_12_out, not_13_out, not_14_out,
       not_15_out;

  not not_1 (not_1_out, In2);
  not not_2 (not_2_out, A1);
  not not_3 (not_3_out, A3);
  not not_4 (not_4_out, In2);
  not not_5 (not_5_out, A1);
  not not_6 (not_6_out, A2);
  not not_7 (not_7_out, In1);
  not not_8 (not_8_out, A1);
  not not_9 (not_9_out, A2);
  not not_10 (not_10_out, In1);
  not not_11 (not_11_out, A1);
  not not_12 (not_12_out, A3);
  not not_13 (not_13_out, In1);
  not not_14 (not_14_out, A2);
  not not_15 (not_15_out, A3);
  and and_1 (N1, not_1_out, not_2_out, A2, not_3_out);
  and and_2 (N2, not_4_out, not_5_out, not_6_out, A3);
  and and_3 (and_3_out, not_7_out, In2, not_8_out, not_9_out);
  and and_4 (and_4_out, not_10_out, In2, not_11_out, not_12_out);
  and and_5 (and_5_out, not_13_out, In2, not_14_out, not_15_out);
  or or_1 (N3, and_3_out, and_4_out, and_5_out);
endmodule
