// Logisim project move.circ as structural Verilog: 1 circuit, main circuit main
module main (
  input  in_1,
  input  [15:0] in_2,
  input  [3:0] in_3,
  output [15:0] out_4
);

  wire [15:0] demultiplexer_1_out0, demultiplexer_1_out1;

  Demultiplexer #(.width(16)) demultiplexer_1 (
    .out0(demultiplexer_1_out0), .out1(demultiplexer_1_out1), .in(in_2), .sel(1'b1), .en(in_3[0]));
  assign out_4 = {demultiplexer_1_out1[14:0], in_1} | demultiplexer_1_out0;  // OR_Gate or_1, 16 bits wide
endmodule
