// Logisim project test.circ as structural Verilog: 1 circuit, main circuit main
module main (
  input  in_1,
  input  in_2,
  input  in_3,
  input  in_4,
  input  in_5,
  input  [1:0] in_6,
  input  in_7,
  input  in_8,
  input  in_9,
  input  in_10,
  input  in_11,
  input  in_12,
  input  [3:0] in_13,
  input  in_14,
  output out_15,
  output out_16,
  output out_17,
  output out_18,
  output out_19,
  output out_20,
  output out_21,
  output out_22,
  output out_23,
  output out_24
);

  Demultiplexer #(.select(2)) demultiplexer_1 (
    .out0(out_20), .out1(out_21), .out2(out_22), .out3(out_23), .in(in_7), .sel(in_13[1:0]), .en(in_8));
  Multiplexer #(.select(2)) multiplexer_1 (
    .in0(in_1), .in1(in_2), .in2(in_3), .in3(in_5), .out(out_15), .sel(in_6), .en(in_4));
  Multiplexer #(.select(2)) multiplexer_2 (
    .in0(in_9), .in1(in_10), .in2(in_11), .in3(in_12), .out(out_24), .sel(in_13[3:2]), .en(in_14));
  Decoder #(.select(2)) decoder_1 (.out0(out_16), .out1(out_17), .out2(out_18), .out3(out_19), .sel(in_6), .en(1'b1));
endmodule
